# Fritzing sketch SimpluURemote_schematic (saved by Fritzing 0.9.3b)
breadboards: 1

parts:
  WeMos_D1_Mini1 = WeMos D1 Mini
  S1_Red = Momentary Switch [package=ksa_sealed_tac_switch]
  S2_White = Momentary Switch [package=ksa_sealed_tac_switch]
  IR_Receiver_TSOP_38KHz = TSOP312.., 314.. [package=THT]
  LED = smd LED [color="Red (633nm)" package="0805 [SMD]"]
  LED_2 = smd LED [color="Infrared (940nm)" package="0805 [SMD]"]
  Transistor_NPN = NPN-Transistor [package="TO92 [THT]"]
  R1 = Resistor [tolerance=±5% resistance=1k package=THT]
  R3 = Resistor [tolerance=±5% resistance=100 package=THT]
  R2 = Resistor [tolerance=±5% resistance=1k package=THT]
  R5 = Resistor [tolerance=±5% resistance=10k package=THT]
  R4 = Resistor [tolerance=±5% resistance=10k package=THT]

nets:
  N1: WeMos_D1_Mini1.3V3, IR_Receiver_TSOP_38KHz.Vs, R5.Pin_0, R4.Pin_0
  N2: WeMos_D1_Mini1.5V, R3.Pin_0
  N3: WeMos_D1_Mini1.D1, R1.Pin_1
  N4: WeMos_D1_Mini1.D2, R2.Pin_0
  N5: WeMos_D1_Mini1.D5, IR_Receiver_TSOP_38KHz.Data
  N6: WeMos_D1_Mini1.D6, S1_Red.2, R4.Pin_1
  N7: WeMos_D1_Mini1.D7, S2_White.2, R5.Pin_1
  GND: WeMos_D1_Mini1.G, S1_Red.3, S2_White.3, IR_Receiver_TSOP_38KHz.GND, LED.cathode, Transistor_NPN.E
  N8: LED.anode, R1.Pin_0
  N9: LED_2.cathode, Transistor_NPN.C
  N10: LED_2.anode, R3.Pin_1
  N11: Transistor_NPN.B, R2.Pin_1
